// Logisim project da1_task2.circ as structural Verilog: 3 circuits, main circuit DUT
module DUT (
  input  IS_SIGNED,
  input  [7:0] D0,
  input  [7:0] D1,
  input  [7:0] D2,
  output [7:0] H,
  output [7:0] M,
  output [7:0] L
);


  // Notes on the sheet:
  //   Please put your deisgn below. You may also use subcircuits.
  //   However, do not move or rename any pins.
endmodule

module TB (
  input  IS_SIGNED,
  input  [7:0] D0,
  input  [7:0] D1,
  input  [7:0] D3,
  output [7:0] H,
  output [7:0] M,
  output [7:0] L
);

  DUT dut_1 (.IS_SIGNED(IS_SIGNED), .D0(D0), .D1(D1), .D2(D3), .H(H), .M(M), .L(L));

  // Notes on the sheet:
  //   DO NOT MODIFY THIS
  //   TEST YOUR CIRCUITS USING THIS TO MAKE SURE YOU HAVE NOT ALTERED PIN OUT
endmodule

module AG_DONOTEDIT (
);

  // Rv32im rv32im_1: pin names not known
  ROM #(.addrWidth(5), .dataWidth(4)) FP ();  // open: addr, data

  // Notes on the sheet:
  //   contents of FP (hex, n*v repeats v):
  //   f 6 0 e 1 2 4 f 6 1 c 6 3 e b 0 f 5 f 7 e 7 a 2 9 7 5 8 f 5 7 a
  //   DO NOT MODIFY THIS
  //   THIS IS FOR AUTOGRADER'S USE - DO NOT TAMPER
endmodule
